// Logisim project D flipflop.circ as structural Verilog: 1 circuit, main circuit main
module main (
);

  wire a_out, and_1_out, and_2_out, and_3_out, and_4_out, and_5_out, and_6_out, and_7_out, and_8_out,
       and_9_out, and_10_out, and_11_out, and_12_out, and_13_out, and_14_out, and_15_out, and_16_out,
       and_17_out, and_18_out, and_19_out, and_20_out, and_21_out, and_22_out, and_23_out, and_24_out,
       and_25_out, and_26_out, and_27_out, and_28_out, and_29_out, and_30_out, and_31_out, and_32_out,
       and_33_out, b_out, c_out, clock_1_out, d_out, e_out, f_out, FFA_q, FFB_q, FFC_q, FFD_q, g_out,
       not_1_out, not_2_out, not_3_out, not_4_out, not_5_out, not_6_out, not_7_out, not_8_out, or_1_out,
       or_2_out, or_3_out, or_4_out;

  Clock clock_1 (.out(clock_1_out));
  D_Flip_Flop FFD (.clk(clock_1_out), .D(or_1_out), .Q(FFD_q));  // open: Qn, preset, en, reset
  D_Flip_Flop FFC (.clk(clock_1_out), .D(or_2_out), .Q(FFC_q));  // open: Qn, preset, en, reset
  D_Flip_Flop FFB (.clk(clock_1_out), .D(or_3_out), .Q(FFB_q));  // open: Qn, preset, en, reset
  D_Flip_Flop FFA (.clk(clock_1_out), .D(or_4_out), .Q(FFA_q));  // open: Qn, preset, en, reset
  not not_1 (not_1_out, FFD_q);
  not not_2 (not_2_out, FFC_q);
  not not_3 (not_3_out, FFB_q);
  not not_4 (not_4_out, FFA_q);
  and and_1 (and_1_out, not_3_out, not_1_out, not_2_out);
  and and_2 (and_2_out, not_4_out, not_1_out, not_2_out);
  and and_3 (and_3_out, not_1_out, FFC_q);
  and and_4 (and_4_out, FFD_q, not_2_out);
  and and_5 (and_5_out, not_3_out, FFA_q);
  and and_6 (and_6_out, not_2_out, FFB_q, not_4_out);
  and and_7 (and_7_out, not_4_out, FFB_q, not_1_out);
  and and_8 (and_8_out, not_3_out, FFC_q, FFD_q);
  or or_1 (or_1_out, and_1_out, and_2_out, and_3_out);
  or or_2 (or_2_out, and_3_out, and_4_out);
  or or_3 (or_3_out, and_6_out, and_7_out, and_8_out);
  and and_9 (and_9_out, FFD_q, FFC_q, FFB_q);
  or or_4 (or_4_out, and_9_out, and_5_out);
  not not_5 (not_5_out, FFA_q);
  not not_6 (not_6_out, FFB_q);
  not not_7 (not_7_out, FFC_q);
  not not_8 (not_8_out, FFD_q);
  and and_10 (and_10_out, FFA_q, not_7_out);
  and and_11 (and_11_out, FFB_q, FFC_q);
  and and_12 (and_12_out, not_5_out, not_6_out, not_8_out);
  and and_13 (and_13_out, FFA_q, FFD_q);
  and and_14 (and_14_out, not_7_out, not_8_out);
  and and_15 (and_15_out, not_5_out, not_7_out, not_8_out);
  and and_16 (and_16_out, not_5_out, FFB_q, not_7_out);
  and and_17 (and_17_out, FFB_q, FFC_q, not_8_out);
  and and_18 (and_18_out, FFA_q, not_6_out);
  and and_19 (and_19_out, not_6_out, not_7_out);
  and and_20 (and_20_out, FFB_q, FFC_q);
  and and_21 (and_21_out, FFA_q, FFB_q);
  and and_22 (and_22_out, not_5_out, not_6_out, not_8_out);
  and and_23 (and_23_out, not_7_out, FFD_q, not_6_out);
  and and_24 (and_24_out, FFB_q, FFC_q);
  and and_25 (and_25_out, not_5_out, not_6_out, not_7_out);
  and and_26 (and_26_out, not_6_out, not_7_out, FFD_q);
  and and_27 (and_27_out, FFB_q, FFC_q, not_8_out);
  and and_28 (and_28_out, FFA_q, FFC_q, not_8_out);
  and and_29 (and_29_out, FFA_q, FFB_q);
  and and_30 (and_30_out, FFB_q, not_7_out, not_8_out);
  and and_31 (and_31_out, FFA_q, not_7_out, not_8_out);
  and and_32 (and_32_out, not_6_out, FFC_q, not_8_out);
  and and_33 (and_33_out, not_5_out, FFC_q, FFD_q);
  or a (a_out, and_10_out, and_11_out, not_8_out);
  or b (b_out, and_12_out, and_13_out, and_14_out, FFB_q);
  or c (c_out, and_15_out, and_16_out, and_17_out, and_18_out);
  or d (d_out, and_19_out, and_20_out, not_8_out);
  or e (e_out, and_21_out, and_22_out, and_23_out, and_24_out);
  or f (f_out, and_25_out, and_26_out, and_27_out, and_28_out);
  or g (g_out, and_29_out, and_30_out, and_31_out, and_32_out, and_33_out);
  _7_Segment_Display u_7_segment_display_1 (
    .g(g_out), .f(f_out), .a(a_out), .b(b_out), .e(e_out), .d(d_out), .c(c_out));  // open: dp
endmodule
