// Logisim project Decoder + D flipflop.circ as structural Verilog: 1 circuit, main circuit main
module main (
  input  in_1
);

  wire and_1_out, and_2_out, and_3_out, and_4_out, and_5_out, and_6_out, and_7_out, and_8_out, and_9_out,
       clock_1_out, decoder_1_out0, decoder_1_out1, decoder_1_out2, decoder_1_out3, decoder_1_out4,
       decoder_1_out5, decoder_1_out6, decoder_1_out7, decoder_1_out8, decoder_1_out9, decoder_1_out10,
       decoder_1_out11, decoder_1_out12, not_1_out, not_2_out, not_3_out, not_4_out, or_1_out, or_2_out,
       or_3_out, or_4_out, or_5_out, or_6_out, or_7_out, or_8_out, or_9_out, or_10_out, or_11_out;
  wire [3:0] FFD_q;

  Clock clock_1 (.out(clock_1_out));
  D_Flip_Flop FFD (.clk(clock_1_out), .D(or_1_out), .Q(FFD_q[0]));  // open: Qn, preset, en, reset
  D_Flip_Flop FFC (.clk(clock_1_out), .D(or_2_out), .Q(FFD_q[1]));  // open: Qn, preset, en, reset
  D_Flip_Flop FFB (.clk(clock_1_out), .D(or_3_out), .Q(FFD_q[2]));  // open: Qn, preset, en, reset
  D_Flip_Flop FFA (.clk(clock_1_out), .D(or_4_out), .Q(FFD_q[3]));  // open: Qn, preset, en, reset
  not not_1 (not_1_out, FFD_q[0]);
  not not_2 (not_2_out, FFD_q[1]);
  not not_3 (not_3_out, FFD_q[2]);
  not not_4 (not_4_out, FFD_q[3]);
  and and_1 (and_1_out, not_3_out, not_1_out, not_2_out);
  and and_2 (and_2_out, not_4_out, not_1_out, not_2_out);
  and and_3 (and_3_out, not_1_out, FFD_q[1]);
  and and_4 (and_4_out, FFD_q[0], not_2_out);
  and and_5 (and_5_out, not_3_out, FFD_q[3]);
  and and_6 (and_6_out, not_2_out, FFD_q[2], not_4_out);
  and and_7 (and_7_out, not_4_out, FFD_q[2], not_1_out);
  and and_8 (and_8_out, not_3_out, FFD_q[1], FFD_q[0]);
  or or_1 (or_1_out, and_1_out, and_2_out, and_3_out);
  or or_2 (or_2_out, and_3_out, and_4_out);
  and and_9 (and_9_out, FFD_q[0], FFD_q[1], FFD_q[2]);
  or or_3 (or_3_out, and_6_out, and_7_out, and_8_out);
  or or_4 (or_4_out, and_9_out, and_5_out);
  Decoder #(.select(4)) decoder_1 (
    .out0(decoder_1_out0), .out1(decoder_1_out1), .out2(decoder_1_out2), .out3(decoder_1_out3),
    .out4(decoder_1_out4), .out5(decoder_1_out5), .out6(decoder_1_out6), .out7(decoder_1_out7),
    .out8(decoder_1_out8), .out9(decoder_1_out9), .out10(decoder_1_out10), .out11(decoder_1_out11),
    .out12(decoder_1_out12), .sel(FFD_q), .en(in_1));  // open: out13, out14, out15
  or or_5 (or_5_out, decoder_1_out0, decoder_1_out2, decoder_1_out4, decoder_1_out6, decoder_1_out7, decoder_1_out8, decoder_1_out9, decoder_1_out10, decoder_1_out12);
  or or_6 (or_6_out, decoder_1_out0, decoder_1_out2, decoder_1_out4, decoder_1_out5, decoder_1_out6, decoder_1_out7, decoder_1_out8, decoder_1_out9, decoder_1_out11, decoder_1_out12);
  or or_7 (or_7_out, decoder_1_out0, decoder_1_out4, decoder_1_out5, decoder_1_out6, decoder_1_out8, decoder_1_out9, decoder_1_out10, decoder_1_out11);
  or or_8 (or_8_out, decoder_1_out0, decoder_1_out1, decoder_1_out2, decoder_1_out4, decoder_1_out6, decoder_1_out7, decoder_1_out8, decoder_1_out9, decoder_1_out10, decoder_1_out12);
  or or_9 (or_9_out, decoder_1_out0, decoder_1_out1, decoder_1_out2, decoder_1_out6, decoder_1_out7, decoder_1_out9, decoder_1_out12);
  or or_10 (or_10_out, decoder_1_out0, decoder_1_out1, decoder_1_out6, decoder_1_out9, decoder_1_out10);
  or or_11 (or_11_out, decoder_1_out2, decoder_1_out3, decoder_1_out4, decoder_1_out7, decoder_1_out8, decoder_1_out10, decoder_1_out12);
  _7_Segment_Display u_7_segment_display_1 (
    .g(or_11_out), .f(or_10_out), .a(or_5_out), .b(or_6_out), .e(or_9_out), .d(or_8_out), .c(or_7_out));  // open: dp
endmodule
