// Logisim project Decoder + JK flipflop.circ as structural Verilog: 1 circuit, main circuit main
module main (
  input  High
);

  wire and_1_out, and_2_out, and_3_out, clock_1_out, decoder_1_out0, decoder_1_out1, decoder_1_out2,
       decoder_1_out3, decoder_1_out4, decoder_1_out5, decoder_1_out6, decoder_1_out7, decoder_1_out8,
       decoder_1_out9, decoder_1_out10, decoder_1_out11, decoder_1_out12, not_1_out, not_2_out, or_1_out,
       or_2_out, or_3_out, or_4_out, or_5_out, or_6_out, or_7_out, or_8_out, or_9_out;
  wire [3:0] FFD_q;

  Clock clock_1 (.out(clock_1_out));
  and and_1 (and_1_out, FFD_q[0], FFD_q[1], FFD_q[2]);
  or or_1 (or_1_out, FFD_q[3], and_3_out);
  J_K_Flip_Flop FFA (.J(and_1_out), .clk(clock_1_out), .K(FFD_q[2]), .Q(FFD_q[3]));  // open: Qn, preset, en, reset
  and and_2 (and_2_out, FFD_q[1], FFD_q[0]);
  and and_3 (and_3_out, FFD_q[1], FFD_q[0]);
  J_K_Flip_Flop FFB (.J(and_2_out), .clk(clock_1_out), .K(or_1_out), .Q(FFD_q[2]));  // open: Qn, preset, en, reset
  not not_1 (not_1_out, FFD_q[3]);
  not not_2 (not_2_out, FFD_q[2]);
  J_K_Flip_Flop FFC (.J(FFD_q[0]), .clk(clock_1_out), .K(FFD_q[0]), .Q(FFD_q[1]));  // open: Qn, preset, en, reset
  or or_2 (or_2_out, not_1_out, not_2_out);
  J_K_Flip_Flop FFD (.J(or_2_out), .clk(clock_1_out), .K(High), .Q(FFD_q[0]));  // open: Qn, preset, en, reset
  Decoder #(.select(4)) decoder_1 (
    .out0(decoder_1_out0), .out1(decoder_1_out1), .out2(decoder_1_out2), .out3(decoder_1_out3),
    .out4(decoder_1_out4), .out5(decoder_1_out5), .out6(decoder_1_out6), .out7(decoder_1_out7),
    .out8(decoder_1_out8), .out9(decoder_1_out9), .out10(decoder_1_out10), .out11(decoder_1_out11),
    .out12(decoder_1_out12), .sel(FFD_q), .en(High));  // open: out13, out14, out15
  or or_3 (or_3_out, decoder_1_out0, decoder_1_out2, decoder_1_out4, decoder_1_out6, decoder_1_out7, decoder_1_out8, decoder_1_out9, decoder_1_out10, decoder_1_out12);
  or or_4 (or_4_out, decoder_1_out0, decoder_1_out2, decoder_1_out4, decoder_1_out5, decoder_1_out6, decoder_1_out7, decoder_1_out8, decoder_1_out9, decoder_1_out11, decoder_1_out12);
  or or_5 (or_5_out, decoder_1_out0, decoder_1_out4, decoder_1_out5, decoder_1_out6, decoder_1_out8, decoder_1_out9, decoder_1_out10, decoder_1_out11);
  or or_6 (or_6_out, decoder_1_out0, decoder_1_out1, decoder_1_out2, decoder_1_out4, decoder_1_out6, decoder_1_out7, decoder_1_out8, decoder_1_out9, decoder_1_out10, decoder_1_out12);
  or or_7 (or_7_out, decoder_1_out0, decoder_1_out1, decoder_1_out2, decoder_1_out6, decoder_1_out7, decoder_1_out9, decoder_1_out12);
  or or_8 (or_8_out, decoder_1_out0, decoder_1_out1, decoder_1_out6, decoder_1_out9, decoder_1_out10);
  or or_9 (or_9_out, decoder_1_out2, decoder_1_out3, decoder_1_out4, decoder_1_out7, decoder_1_out8, decoder_1_out10, decoder_1_out12);
  _7_Segment_Display u_7_segment_display_1 (
    .g(or_9_out), .f(or_8_out), .a(or_3_out), .b(or_4_out), .e(or_7_out), .d(or_6_out), .c(or_5_out));  // open: dp
endmodule
