// Logisim project Decoder + T flipflop.circ as structural Verilog: 1 circuit, main circuit main
module main (
  input  in_1
);

  wire a_2_out, and_1_out, and_2_out, and_3_out, and_4_out, b_2_out, c_2_out, clock_1_out, d_2_out,
       decoder_1_out0, decoder_1_out1, decoder_1_out2, decoder_1_out3, decoder_1_out4, decoder_1_out5,
       decoder_1_out6, decoder_1_out7, decoder_1_out8, decoder_1_out9, decoder_1_out10, decoder_1_out11,
       decoder_1_out12, e_out, f_out, g_out, not_1_out, not_2_out, or_1_out, or_2_out, or_3_out;
  wire [3:0] D_q;

  or or_1 (or_1_out, not_2_out, not_1_out);
  Clock clock_1 (.out(clock_1_out));
  T_Flip_Flop D (.clk(clock_1_out), .T(or_1_out), .Q(D_q[0]));  // open: Qn, preset, reset, en
  T_Flip_Flop C (.clk(clock_1_out), .T(D_q[0]), .Q(D_q[1]));  // open: Qn, preset, reset, en
  T_Flip_Flop B (.clk(clock_1_out), .T(or_2_out), .Q(D_q[2]));  // open: Qn, preset, reset, en
  T_Flip_Flop A (.clk(clock_1_out), .T(or_3_out), .Q(D_q[3]));  // open: Qn, preset, reset, en
  not not_1 (not_1_out, D_q[2]);
  not not_2 (not_2_out, D_q[3]);
  and and_1 (and_1_out, D_q[0], D_q[1]);
  and and_2 (and_2_out, D_q[3], D_q[2]);
  and and_3 (and_3_out, D_q[2], D_q[3]);
  and and_4 (and_4_out, D_q[2], D_q[1], D_q[0]);
  or or_2 (or_2_out, and_1_out, and_2_out);
  or or_3 (or_3_out, and_3_out, and_4_out);
  Decoder #(.select(4)) decoder_1 (
    .out0(decoder_1_out0), .out1(decoder_1_out1), .out2(decoder_1_out2), .out3(decoder_1_out3),
    .out4(decoder_1_out4), .out5(decoder_1_out5), .out6(decoder_1_out6), .out7(decoder_1_out7),
    .out8(decoder_1_out8), .out9(decoder_1_out9), .out10(decoder_1_out10), .out11(decoder_1_out11),
    .out12(decoder_1_out12), .sel(D_q), .en(in_1));  // open: out13, out14, out15
  or a_2 (a_2_out, decoder_1_out0, decoder_1_out2, decoder_1_out4, decoder_1_out6, decoder_1_out7, decoder_1_out8, decoder_1_out9, decoder_1_out10, decoder_1_out12);
  or b_2 (b_2_out, decoder_1_out0, decoder_1_out2, decoder_1_out4, decoder_1_out5, decoder_1_out6, decoder_1_out7, decoder_1_out8, decoder_1_out9, decoder_1_out11, decoder_1_out12);
  or c_2 (c_2_out, decoder_1_out0, decoder_1_out4, decoder_1_out5, decoder_1_out6, decoder_1_out8, decoder_1_out9, decoder_1_out10, decoder_1_out11);
  or d_2 (d_2_out, decoder_1_out0, decoder_1_out1, decoder_1_out2, decoder_1_out4, decoder_1_out6, decoder_1_out7, decoder_1_out8, decoder_1_out9, decoder_1_out10, decoder_1_out12);
  or e (e_out, decoder_1_out0, decoder_1_out1, decoder_1_out2, decoder_1_out6, decoder_1_out7, decoder_1_out9, decoder_1_out12);
  or f (f_out, decoder_1_out0, decoder_1_out1, decoder_1_out6, decoder_1_out9, decoder_1_out10);
  or g (g_out, decoder_1_out2, decoder_1_out3, decoder_1_out4, decoder_1_out7, decoder_1_out8, decoder_1_out10, decoder_1_out12);
  _7_Segment_Display u_7_segment_display_1 (
    .g(g_out), .f(f_out), .a(a_2_out), .b(b_2_out), .e(e_out), .d(d_2_out), .c(c_2_out));  // open: dp
endmodule
