// Logisim project MUX + D flipflop.circ as structural Verilog: 1 circuit, main circuit main
module main (
  input  _1
);

  wire A_qn, and_1_out, and_2_out, and_3_out, and_4_out, and_5_out, and_6_out, and_7_out, B_qn, C_qn,
       clock_1_out, D_q, D_qn, multiplexer_1_out, multiplexer_2_out, multiplexer_3_out, multiplexer_4_out,
       multiplexer_5_out, multiplexer_6_out, multiplexer_7_out, not_1_out, not_2_out, or_1_out, or_2_out,
       or_3_out, xor_1_out;
  wire [2:0] C_q;

  Clock clock_1 (.out(clock_1_out));
  D_Flip_Flop A (.clk(clock_1_out), .D(or_1_out), .Q(C_q[2]), .Qn(A_qn));  // open: preset, en, reset
  D_Flip_Flop B (.clk(clock_1_out), .D(or_3_out), .Q(C_q[1]), .Qn(B_qn));  // open: preset, en, reset
  D_Flip_Flop C (.clk(clock_1_out), .D(xor_1_out), .Q(C_q[0]), .Qn(C_qn));  // open: preset, en, reset
  D_Flip_Flop D (.clk(clock_1_out), .D(or_2_out), .Q(D_q), .Qn(D_qn));  // open: preset, en, reset
  and and_1 (and_1_out, C_q[2], B_qn);
  and and_2 (and_2_out, C_q[1], C_q[0], D_q);
  and and_3 (and_3_out, A_qn, C_q[1], C_qn);
  and and_4 (and_4_out, A_qn, C_q[1], D_qn);
  and and_5 (and_5_out, B_qn, C_q[0], D_q);
  xor xor_1 (xor_1_out, C_q[0], D_q);
  and and_6 (and_6_out, B_qn, D_qn);
  and and_7 (and_7_out, A_qn, C_q[1], D_qn);
  or or_1 (or_1_out, and_1_out, and_2_out);
  or or_2 (or_2_out, and_6_out, and_7_out);
  or or_3 (or_3_out, and_3_out, and_4_out, and_5_out);
  not not_1 (not_1_out, D_q);
  not not_2 (not_2_out, _1);
  Multiplexer #(.select(3)) multiplexer_1 (
    .in0(not_1_out), .in1(not_1_out), .in2(not_1_out), .in3(_1), .in4(_1), .in5(not_1_out), .in6(not_1_out),
    .in7(not_2_out), .out(multiplexer_1_out), .sel(C_q), .en(_1));
  Multiplexer #(.select(3)) multiplexer_2 (
    .in0(not_1_out), .in1(not_1_out), .in2(_1), .in3(_1), .in4(_1), .in5(D_q), .in6(not_1_out),
    .in7(not_2_out), .out(multiplexer_2_out), .sel(C_q), .en(_1));
  Multiplexer #(.select(3)) multiplexer_3 (
    .in0(not_1_out), .in1(not_2_out), .in2(_1), .in3(not_1_out), .in4(_1), .in5(_1), .in6(not_2_out),
    .in7(not_2_out), .out(multiplexer_3_out), .sel(C_q), .en(_1));
  Multiplexer #(.select(3)) multiplexer_4 (
    .in0(_1), .in1(not_1_out), .in2(not_1_out), .in3(_1), .in4(_1), .in5(not_1_out), .in6(not_1_out),
    .in7(not_2_out), .out(multiplexer_4_out), .sel(C_q), .en(_1));
  Multiplexer #(.select(3)) multiplexer_5 (
    .in0(_1), .in1(not_1_out), .in2(not_2_out), .in3(_1), .in4(D_q), .in5(not_2_out), .in6(not_1_out),
    .in7(not_2_out), .out(multiplexer_5_out), .sel(C_q), .en(_1));
  Multiplexer #(.select(3)) multiplexer_6 (
    .in0(_1), .in1(not_2_out), .in2(not_2_out), .in3(not_1_out), .in4(D_q), .in5(not_1_out), .in6(not_2_out),
    .in7(not_2_out), .out(multiplexer_6_out), .sel(C_q), .en(_1));
  Multiplexer #(.select(3)) multiplexer_7 (
    .in0(not_2_out), .in1(_1), .in2(not_1_out), .in3(D_q), .in4(not_1_out), .in5(not_1_out), .in6(not_1_out),
    .in7(not_2_out), .out(multiplexer_7_out), .sel(C_q), .en(_1));
  _7_Segment_Display u_7_segment_display_1 (
    .g(multiplexer_7_out), .f(multiplexer_6_out), .a(multiplexer_1_out), .b(multiplexer_2_out),
    .e(multiplexer_5_out), .d(multiplexer_4_out), .c(multiplexer_3_out));  // open: dp
endmodule
