// Logisim project MUX + JK flipflop.circ as structural Verilog: 1 circuit, main circuit main
module main (
  input  _1,
  input  _0
);

  wire and_1_out, and_2_out, and_3_out, clock_1_out, FFA_qn, FFB_qn, FFD_q, multiplexer_1_out,
       multiplexer_2_out, multiplexer_3_out, multiplexer_4_out, multiplexer_5_out, multiplexer_6_out,
       multiplexer_7_out, not_1_out, or_1_out, or_2_out;
  wire [2:0] FFC_q;

  Clock clock_1 (.out(clock_1_out));
  J_K_Flip_Flop FFA (
    .J(and_1_out), .clk(clock_1_out), .K(FFC_q[1]), .Q(FFC_q[2]), .Qn(FFA_qn));  // open: preset, en, reset
  J_K_Flip_Flop FFB (
    .J(and_2_out), .clk(clock_1_out), .K(or_2_out), .Q(FFC_q[1]), .Qn(FFB_qn));  // open: preset, en, reset
  J_K_Flip_Flop FFC (.J(FFD_q), .clk(clock_1_out), .K(FFD_q), .Q(FFC_q[0]));  // open: Qn, preset, en, reset
  J_K_Flip_Flop FFD (.J(or_1_out), .clk(clock_1_out), .K(_1), .Q(FFD_q));  // open: Qn, preset, en, reset
  and and_1 (and_1_out, FFD_q, FFC_q[0], FFC_q[1]);
  and and_2 (and_2_out, FFC_q[0], FFD_q);
  and and_3 (and_3_out, FFC_q[0], FFD_q);
  or or_1 (or_1_out, FFB_qn, FFA_qn);
  or or_2 (or_2_out, and_3_out, FFC_q[2]);
  not not_1 (not_1_out, FFD_q);
  Multiplexer #(.select(3)) multiplexer_1 (
    .in0(not_1_out), .in1(not_1_out), .in2(not_1_out), .in3(_1), .in4(_1), .in5(not_1_out), .in6(not_1_out),
    .out(multiplexer_1_out), .sel(FFC_q), .en(_1));  // open: in7
  Multiplexer #(.select(3)) multiplexer_2 (
    .in0(not_1_out), .in1(not_1_out), .in2(_1), .in3(_1), .in4(_1), .in5(FFD_q), .in6(not_1_out),
    .out(multiplexer_2_out), .sel(FFC_q), .en(_1));  // open: in7
  Multiplexer #(.select(3)) multiplexer_3 (
    .in0(not_1_out), .in1(_0), .in2(_1), .in3(not_1_out), .in4(_1), .in5(_1), .in6(_0),
    .out(multiplexer_3_out), .sel(FFC_q), .en(_1));  // open: in7
  Multiplexer #(.select(3)) multiplexer_4 (
    .in0(_1), .in1(not_1_out), .in2(not_1_out), .in3(_1), .in4(_1), .in5(not_1_out), .in6(not_1_out),
    .out(multiplexer_4_out), .sel(FFC_q), .en(_1));  // open: in7
  Multiplexer #(.select(3)) multiplexer_5 (
    .in0(_1), .in1(not_1_out), .in2(_0), .in3(_1), .in4(FFD_q), .in5(_0), .in6(not_1_out),
    .out(multiplexer_5_out), .sel(FFC_q), .en(_1));  // open: in7
  Multiplexer #(.select(3)) multiplexer_6 (
    .in0(_1), .in1(_0), .in2(_0), .in3(not_1_out), .in4(FFD_q), .in5(not_1_out), .in6(_0),
    .out(multiplexer_6_out), .sel(FFC_q), .en(_1));  // open: in7
  Multiplexer #(.select(3)) multiplexer_7 (
    .in0(_0), .in1(_1), .in2(not_1_out), .in3(FFD_q), .in4(not_1_out), .in5(not_1_out), .in6(not_1_out),
    .out(multiplexer_7_out), .sel(FFC_q), .en(_1));  // open: in7
  _7_Segment_Display u_7_segment_display_1 (
    .g(multiplexer_7_out), .f(multiplexer_6_out), .a(multiplexer_1_out), .b(multiplexer_2_out),
    .e(multiplexer_5_out), .d(multiplexer_4_out), .c(multiplexer_3_out));  // open: dp
endmodule
