// Logisim project MUX + T flipflop.circ as structural Verilog: 1 circuit, main circuit main
module main (
  input  _1,
  input  _0
);

  wire and_1_out, and_2_out, and_3_out, and_4_out, clock_1_out, D_q, multiplexer_1_out, multiplexer_2_out,
       multiplexer_3_out, multiplexer_4_out, multiplexer_5_out, multiplexer_6_out, multiplexer_7_out,
       not_1_out, not_2_out, not_3_out, or_1_out, or_2_out, or_3_out;
  wire [2:0] C_q;

  or or_1 (or_1_out, not_2_out, not_1_out);
  Clock clock_1 (.out(clock_1_out));
  T_Flip_Flop D (.clk(clock_1_out), .T(or_1_out), .Q(D_q));  // open: Qn, preset, reset, en
  T_Flip_Flop C (.clk(clock_1_out), .T(D_q), .Q(C_q[0]));  // open: Qn, preset, reset, en
  not not_1 (not_1_out, C_q[1]);
  T_Flip_Flop B (.clk(clock_1_out), .T(or_2_out), .Q(C_q[1]));  // open: Qn, preset, reset, en
  not not_2 (not_2_out, C_q[2]);
  T_Flip_Flop A (.clk(clock_1_out), .T(or_3_out), .Q(C_q[2]));  // open: Qn, preset, reset, en
  and and_1 (and_1_out, D_q, C_q[0]);
  and and_2 (and_2_out, C_q[2], C_q[1]);
  and and_3 (and_3_out, C_q[1], C_q[2]);
  and and_4 (and_4_out, C_q[1], C_q[0], D_q);
  or or_2 (or_2_out, and_1_out, and_2_out);
  or or_3 (or_3_out, and_3_out, and_4_out);
  not not_3 (not_3_out, D_q);
  Multiplexer #(.select(3)) multiplexer_1 (
    .in0(not_3_out), .in1(not_3_out), .in2(not_3_out), .in3(_1), .in4(_1), .in5(not_3_out), .in6(not_3_out),
    .in7(_0), .out(multiplexer_1_out), .sel(C_q), .en(_1));
  Multiplexer #(.select(3)) multiplexer_2 (
    .in0(not_3_out), .in1(not_3_out), .in2(_1), .in3(_1), .in4(_1), .in5(D_q), .in6(not_3_out), .in7(_0),
    .out(multiplexer_2_out), .sel(C_q), .en(_1));
  Multiplexer #(.select(3)) multiplexer_3 (
    .in0(not_3_out), .in1(_0), .in2(_1), .in3(not_3_out), .in4(_1), .in5(_1), .in6(_0), .in7(_0),
    .out(multiplexer_3_out), .sel(C_q), .en(_1));
  Multiplexer #(.select(3)) multiplexer_4 (
    .in0(_1), .in1(not_3_out), .in2(not_3_out), .in3(_1), .in4(_1), .in5(not_3_out), .in6(not_3_out),
    .in7(_0), .out(multiplexer_4_out), .sel(C_q), .en(_1));
  Multiplexer #(.select(3)) multiplexer_5 (
    .in0(_1), .in1(not_3_out), .in2(_0), .in3(_1), .in4(D_q), .in5(_0), .in6(not_3_out), .in7(_0),
    .out(multiplexer_5_out), .sel(C_q), .en(_1));
  Multiplexer #(.select(3)) multiplexer_6 (
    .in0(_1), .in1(_0), .in2(_0), .in3(not_3_out), .in4(D_q), .in5(not_3_out), .in6(_0), .in7(_0),
    .out(multiplexer_6_out), .sel(C_q), .en(_1));
  Multiplexer #(.select(3)) multiplexer_7 (
    .in0(_0), .in1(_1), .in2(not_3_out), .in3(D_q), .in4(not_3_out), .in5(not_3_out), .in6(not_3_out),
    .in7(_0), .out(multiplexer_7_out), .sel(C_q), .en(_1));
  _7_Segment_Display u_7_segment_display_1 (
    .g(multiplexer_7_out), .f(multiplexer_6_out), .a(multiplexer_1_out), .b(multiplexer_2_out),
    .e(multiplexer_5_out), .d(multiplexer_4_out), .c(multiplexer_3_out));  // open: dp
endmodule
