// Logisim project MUX.circ as structural Verilog: 1 circuit, main circuit main
module main (
  input  [2:0] ABC,
  input  D,
  input  _1,
  input  _0
);

  wire multiplexer_1_out, multiplexer_2_out, multiplexer_3_out, multiplexer_4_out, multiplexer_5_out,
       multiplexer_6_out, multiplexer_7_out, not_1_out;

  not not_1 (not_1_out, D);
  Multiplexer #(.select(3)) multiplexer_1 (
    .in0(not_1_out), .in1(not_1_out), .in2(not_1_out), .in3(_1), .in4(_1), .in5(not_1_out), .in6(not_1_out),
    .in7(_0), .out(multiplexer_1_out), .sel(ABC), .en(_1));
  Multiplexer #(.select(3)) multiplexer_2 (
    .in0(not_1_out), .in1(not_1_out), .in2(_1), .in3(_1), .in4(_1), .in5(D), .in6(not_1_out), .in7(_0),
    .out(multiplexer_2_out), .sel(ABC), .en(_1));
  Multiplexer #(.select(3)) multiplexer_3 (
    .in0(not_1_out), .in1(_0), .in2(_1), .in3(not_1_out), .in4(_1), .in5(_1), .in6(_0), .in7(_0),
    .out(multiplexer_3_out), .sel(ABC), .en(_1));
  Multiplexer #(.select(3)) multiplexer_4 (
    .in0(_1), .in1(not_1_out), .in2(not_1_out), .in3(_1), .in4(_1), .in5(not_1_out), .in6(not_1_out),
    .in7(_0), .out(multiplexer_4_out), .sel(ABC), .en(_1));
  Multiplexer #(.select(3)) multiplexer_5 (
    .in0(_1), .in1(not_1_out), .in2(_0), .in3(_1), .in4(D), .in5(_0), .in6(not_1_out), .in7(_0),
    .out(multiplexer_5_out), .sel(ABC), .en(_1));
  Multiplexer #(.select(3)) multiplexer_6 (
    .in0(_1), .in1(_0), .in2(_0), .in3(not_1_out), .in4(D), .in5(not_1_out), .in6(_0), .in7(_0),
    .out(multiplexer_6_out), .sel(ABC), .en(_1));
  Multiplexer #(.select(3)) multiplexer_7 (
    .in0(_0), .in1(_1), .in2(not_1_out), .in3(D), .in4(not_1_out), .in5(not_1_out), .in6(not_1_out),
    .in7(_0), .out(multiplexer_7_out), .sel(ABC), .en(_1));
  _7_Segment_Display u_7_segment_display_1 (
    .g(multiplexer_7_out), .f(multiplexer_6_out), .a(multiplexer_1_out), .b(multiplexer_2_out),
    .e(multiplexer_5_out), .d(multiplexer_4_out), .c(multiplexer_3_out));  // open: dp
endmodule
