// Logisim project T flipflop.circ as structural Verilog: 1 circuit, main circuit main
module main (
);

  wire a_2_out, A_q, and_1_out, and_2_out, and_3_out, and_4_out, and_5_out, and_6_out, and_7_out, and_8_out,
       and_9_out, and_10_out, and_11_out, and_12_out, and_13_out, and_14_out, and_15_out, and_16_out,
       and_17_out, and_18_out, and_19_out, and_20_out, and_21_out, and_22_out, and_23_out, and_24_out,
       and_25_out, and_26_out, and_27_out, and_28_out, b_2_out, B_q, c_2_out, C_q, clock_1_out, d_2_out, D_q,
       e_out, f_out, g_out, not_1_out, not_2_out, not_3_out, not_4_out, not_5_out, not_6_out, or_1_out,
       or_2_out, or_3_out;

  or or_1 (or_1_out, not_2_out, not_1_out);
  Clock clock_1 (.out(clock_1_out));
  T_Flip_Flop D (.clk(clock_1_out), .T(or_1_out), .Q(D_q));  // open: Qn, preset, reset, en
  T_Flip_Flop C (.clk(clock_1_out), .T(D_q), .Q(C_q));  // open: Qn, preset, reset, en
  not not_1 (not_1_out, B_q);
  T_Flip_Flop B (.clk(clock_1_out), .T(or_3_out), .Q(B_q));  // open: Qn, preset, reset, en
  not not_2 (not_2_out, A_q);
  T_Flip_Flop A (.clk(clock_1_out), .T(or_2_out), .Q(A_q));  // open: Qn, preset, reset, en
  and and_1 (and_1_out, B_q, A_q);
  and and_2 (and_2_out, B_q, C_q, D_q);
  and and_3 (and_3_out, D_q, C_q);
  and and_4 (and_4_out, A_q, B_q);
  or or_2 (or_2_out, and_1_out, and_2_out);
  or or_3 (or_3_out, and_3_out, and_4_out);
  not not_3 (not_3_out, A_q);
  not not_4 (not_4_out, B_q);
  not not_5 (not_5_out, C_q);
  not not_6 (not_6_out, D_q);
  and and_5 (and_5_out, A_q, not_5_out);
  and and_6 (and_6_out, B_q, C_q);
  and and_7 (and_7_out, not_3_out, not_4_out, not_6_out);
  and and_8 (and_8_out, A_q, D_q);
  and and_9 (and_9_out, not_5_out, not_6_out);
  and and_10 (and_10_out, not_3_out, not_5_out, not_6_out);
  and and_11 (and_11_out, not_3_out, B_q, not_5_out);
  and and_12 (and_12_out, B_q, C_q, not_6_out);
  and and_13 (and_13_out, A_q, not_4_out);
  and and_14 (and_14_out, not_4_out, not_5_out);
  and and_15 (and_15_out, B_q, C_q);
  and and_16 (and_16_out, A_q, B_q);
  and and_17 (and_17_out, not_3_out, not_4_out, not_6_out);
  and and_18 (and_18_out, not_5_out, D_q, not_4_out);
  and and_19 (and_19_out, B_q, C_q);
  and and_20 (and_20_out, not_3_out, not_4_out, not_5_out);
  and and_21 (and_21_out, not_4_out, not_5_out, D_q);
  and and_22 (and_22_out, B_q, C_q, not_6_out);
  and and_23 (and_23_out, A_q, C_q, not_6_out);
  and and_24 (and_24_out, A_q, B_q);
  and and_25 (and_25_out, B_q, not_5_out, not_6_out);
  and and_26 (and_26_out, A_q, not_5_out, not_6_out);
  and and_27 (and_27_out, not_4_out, C_q, not_6_out);
  and and_28 (and_28_out, not_3_out, C_q, D_q);
  or a_2 (a_2_out, and_5_out, and_6_out, not_6_out);
  or b_2 (b_2_out, and_7_out, and_8_out, and_9_out, B_q);
  or c_2 (c_2_out, and_10_out, and_11_out, and_12_out, and_13_out);
  or d_2 (d_2_out, and_14_out, and_15_out, not_6_out);
  or e (e_out, and_16_out, and_17_out, and_18_out, and_19_out);
  or f (f_out, and_20_out, and_21_out, and_22_out, and_23_out);
  or g (g_out, and_24_out, and_25_out, and_26_out, and_27_out, and_28_out);
  _7_Segment_Display u_7_segment_display_1 (
    .g(g_out), .f(f_out), .a(a_2_out), .b(b_2_out), .e(e_out), .d(d_2_out), .c(c_2_out));  // open: dp
endmodule
